// Logisim project LC-2200-16.circ as structural Verilog: 2 circuits, main circuit my circuit
module my_circuit (
);

  wire CLK_prime, DrALU, DrPC, LdA, LdB, LdPC;
  wire [1:0] func;
  wire [15:0] A_q, ALU_out, B_q, controlled_buffer_1_out, controlled_buffer_2_out, PC_q, undriven;

  Register #(.width(16)) PC (.D(undriven), .en(LdPC), .Q(PC_q), .clk(CLK_prime));  // open: clr
  assign controlled_buffer_1_out = DrPC ? PC_q : 16'bz;  // Controlled_Buffer controlled_buffer_1
  Register #(.width(16)) A (.D(undriven), .en(LdA), .Q(A_q), .clk(CLK_prime));  // open: clr
  Register #(.width(16)) B (.D(undriven), .en(LdB), .Q(B_q), .clk(CLK_prime));  // open: clr
  ALU ALU (.func(func), .A(A_q), .B(B_q), .OUT(ALU_out));
  assign controlled_buffer_2_out = DrALU ? ALU_out : 16'bz;  // Controlled_Buffer controlled_buffer_2
endmodule

module ALU (
  input  [15:0] A,
  input  [15:0] B,
  input  [1:0] func,
  output [15:0] OUT
);

  wire [15:0] ADD, AND, plus_1, SUB;

  Adder #(.width(16)) adder_1 (.a(A), .b(B), .out(ADD));  // open: cin, cout
  Subtractor #(.width(16)) subtractor_1 (.a(A), .b(B), .out(SUB));  // open: bin, bout
  Multiplexer #(.select(2), .width(16), .disabled(0), .enable("false")) multiplexer_1 (
    .in0(ADD), .in1(AND), .in2(SUB), .in3(plus_1), .out(OUT), .sel(func));
  assign AND = ~(A & B);  // NAND_Gate nand_1, 16 bits wide
  Adder #(.width(16)) adder_2 (.a(A), .b(16'h1), .out(plus_1));  // open: cin, cout
endmodule
